// Logisim project Julia_ChaparroV2.circ as structural Verilog: 15 circuits, main circuit main
module main (
  output [15:0] out_1
);

  wire and_1_out, comparator_1_eq, comparator_2_eq, data_addr, Flags_out_6, Flags_out_7, Flags_out_8,
       Flags_out_9, in_out, io_e, io_s, keyboard_1_avail, or_1_out, register_1_q, register_2_q, t_ff_1_q,
       uc_1_inf, uc_1_ir_set, uc_1_r0_e, uc_1_r0_s, uc_1_r1_e, uc_1_r1_s, uc_1_r2_e, uc_1_r2_s, uc_1_r3_e,
       uc_1_r3_s, uc_1_to_acc_e, uc_1_to_acc_s, uc_1_to_bus, uc_1_to_flag_s, uc_1_to_iar_e, uc_1_to_iar_s,
       uc_1_to_mar_s, uc_1_to_ram_e, uc_1_to_ram_s, uc_1_to_tmp_s, ula_1_a_igual_b, ula_1_a_maior,
       ula_1_carry_out, ula_1_zero;
  wire [2:0] uc_1_ula_op;
  wire [6:0] bit_extender_2_out, keyboard_1_data;
  wire [15:0] ACC_q, bit_extender_1_out, Bus_1_out_3, controlled_buffer_1_out, IAR_q, IR_q, MAR_q, R0_q,
       R1_q, R2_q, R3_q, TMP_q, ula_1_out_5;

  Register #(.width(16)) TMP (.D(controlled_buffer_1_out), .Q(TMP_q), .clk(uc_1_to_tmp_s));  // open: en, clr
  bus1 Bus_1 (.in_1(TMP_q), .out_3(Bus_1_out_3), .in_2(uc_1_to_bus));
  ULA ula_1 (
    .A(controlled_buffer_1_out), .B(Bus_1_out_3), .out_5(ula_1_out_5), .in_1(uc_1_ula_op),
    .carry_out(ula_1_carry_out), .A_maior(ula_1_a_maior), .a_igual_b(ula_1_a_igual_b), .zero(ula_1_zero));
  Register #(.width(16)) ACC (.D(ula_1_out_5), .Q(ACC_q), .clk(uc_1_to_acc_s));  // open: en, clr
  Comparator #(.width(16)) comparator_1 (
    .a(controlled_buffer_1_out), .b(16'hff97), .eq(comparator_1_eq));  // open: gt, lt
  and and_1 (and_1_out, io_s, data_addr, in_out);
  Flag Flags (
    .in_1(ula_1_carry_out), .in_2(ula_1_a_maior), .in_3(ula_1_a_igual_b), .in_4(ula_1_zero),
    .out_6(Flags_out_6), .out_7(Flags_out_7), .out_8(Flags_out_8), .out_9(Flags_out_9), .in_5(uc_1_to_flag_s));
  assign controlled_buffer_1_out = uc_1_to_acc_e ? ACC_q : 16'bz;  // Controlled_Buffer controlled_buffer_1
  T_Flip_Flop t_ff_1 (.clk(io_e), .T(keyboard_1_avail), .Q(t_ff_1_q));  // open: Qn, preset, reset
  Keyboard #(.trigger("falling")) keyboard_1 (
    .clk(t_ff_1_q), .re(register_1_q), .avail(keyboard_1_avail), .data(keyboard_1_data));  // open: clr
  Register #(.width(1)) register_1 (.D(comparator_1_eq), .Q(register_1_q), .clk(and_1_out));  // open: en, clr
  assign controlled_buffer_1_out = uc_1_r0_e ? R0_q : 16'bz;  // Controlled_Buffer controlled_buffer_2
  Register #(.width(16)) R0 (.D(controlled_buffer_1_out), .Q(R0_q), .clk(uc_1_r0_s));  // open: en, clr
  assign bit_extender_1_out = {{9{1'b0}}, keyboard_1_data};  // Bit_Extender bit_extender_1
  assign controlled_buffer_1_out = t_ff_1_q ? bit_extender_1_out : 16'bz;  // Controlled_Buffer controlled_buffer_3
  assign controlled_buffer_1_out = uc_1_r1_e ? R1_q : 16'bz;  // Controlled_Buffer controlled_buffer_4
  Register #(.width(16)) R1 (.D(controlled_buffer_1_out), .Q(R1_q), .clk(uc_1_r1_s));  // open: en, clr
  Register #(.width(16)) IAR (.D(controlled_buffer_1_out), .Q(IAR_q), .clk(uc_1_to_iar_s));  // open: en, clr
  assign controlled_buffer_1_out = uc_1_to_iar_e ? IAR_q : 16'bz;  // Controlled_Buffer controlled_buffer_5
  assign controlled_buffer_1_out = uc_1_r2_e ? R2_q : 16'bz;  // Controlled_Buffer controlled_buffer_6
  Register #(.width(16)) R2 (.D(controlled_buffer_1_out), .Q(R2_q), .clk(uc_1_r2_s));  // open: en, clr
  UC uc_1 (
    .ULA_OP(uc_1_ula_op), .from_carry_out(Flags_out_6), .flag_a_larger(Flags_out_7), .reg_equal(Flags_out_8),
    .reg_zero(Flags_out_9), .to_flag_s(uc_1_to_flag_s), .to_bus(uc_1_to_bus), .to_tmp_s(uc_1_to_tmp_s),
    .r0_s(uc_1_r0_s), .r0_e(uc_1_r0_e), .r1_s(uc_1_r1_s), .r1_e(uc_1_r1_e), .r2_s(uc_1_r2_s),
    .r2_e(uc_1_r2_e), .r3_s(uc_1_r3_s), .r3_e(uc_1_r3_e), .to_mar_s(uc_1_to_mar_s), .to_acc_s(uc_1_to_acc_s),
    .to_acc_e(uc_1_to_acc_e), .to_iar_s(uc_1_to_iar_s), .to_iar_e(uc_1_to_iar_e), .in_5(IR_q),
    .ir_set(uc_1_ir_set), .input_output(in_out), .data_address(data_addr), .to_io_e(io_e), .to_io_s(io_s),
    .to_ram_s(uc_1_to_ram_s), .to_ram_e(uc_1_to_ram_e), .inf(uc_1_inf));
  LED led_1 (.in(uc_1_inf));
  Register #(.width(16)) IR (.D(controlled_buffer_1_out), .Q(IR_q), .clk(uc_1_ir_set));  // open: en, clr
  Comparator #(.width(16)) comparator_2 (
    .a(controlled_buffer_1_out), .b(16'hff98), .eq(comparator_2_eq));  // open: gt, lt
  assign controlled_buffer_1_out = uc_1_r3_e ? R3_q : 16'bz;  // Controlled_Buffer controlled_buffer_7
  Register #(.width(16)) R3 (.D(controlled_buffer_1_out), .Q(R3_q), .clk(uc_1_r3_s));  // open: en, clr
  Register #(.width(1)) register_2 (.D(comparator_2_eq), .Q(register_2_q), .clk(and_1_out));  // open: en, clr
  Register #(.width(16)) MAR (.D(controlled_buffer_1_out), .Q(MAR_q), .clk(uc_1_to_mar_s));  // open: en, clr
  or or_1 (or_1_out, uc_1_to_ram_e, uc_1_to_ram_s);
  Bit_Extender #(.in_width(16), .out_width(7), .\type ("zero")) bit_extender_2 (
    .in(controlled_buffer_1_out), .out(bit_extender_2_out));
  TTY tty_1 (.data(bit_extender_2_out), .clk(io_s), .we(register_2_q));  // open: clr
  RAM #(.addrWidth(16), .dataWidth(16), .\type ("nonvolatile")) ram_1 (
    .addr(MAR_q), .we(uc_1_to_ram_s), .oe(uc_1_to_ram_e), .clk(or_1_out), .din(controlled_buffer_1_out),
    .dout(out_1));
  assign controlled_buffer_1_out = uc_1_to_ram_e ? out_1 : 16'bz;  // Controlled_Buffer controlled_buffer_8
endmodule

module somador_1bit (
  input  a,
  input  b,
  input  c_in,
  output o,
  output c_out
);

  wire and_1_out, and_2_out, and_3_out, xor_1_out;

  xor xor_1 (xor_1_out, a, b);
  xor xor_2 (o, xor_1_out, c_in);
  and and_1 (and_1_out, a, c_in);
  and and_2 (and_2_out, a, b);
  and and_3 (and_3_out, b, c_in);
  or or_1 (c_out, and_1_out, and_2_out, and_3_out);
endmodule

module somador_8bits (
  input  in_1,
  input  [7:0] a,
  input  [7:0] b,
  output [7:0] saida,
  output out_5
);

  wire somador_1bit_1_c_out, somador_1bit_2_c_out, somador_1bit_3_c_out, somador_1bit_4_c_out,
       somador_1bit_5_c_out, somador_1bit_6_c_out, somador_1bit_7_c_out;

  somador_1bit somador_1bit_1 (.a(a[0]), .b(b[0]), .c_in(in_1), .o(saida[0]), .c_out(somador_1bit_1_c_out));
  somador_1bit somador_1bit_2 (
    .a(a[1]), .b(b[1]), .c_in(somador_1bit_1_c_out), .o(saida[1]), .c_out(somador_1bit_2_c_out));
  somador_1bit somador_1bit_3 (
    .a(a[2]), .b(b[2]), .c_in(somador_1bit_2_c_out), .o(saida[2]), .c_out(somador_1bit_3_c_out));
  somador_1bit somador_1bit_4 (
    .a(a[3]), .b(b[3]), .c_in(somador_1bit_3_c_out), .o(saida[3]), .c_out(somador_1bit_4_c_out));
  somador_1bit somador_1bit_5 (
    .a(a[4]), .b(b[4]), .c_in(somador_1bit_4_c_out), .o(saida[4]), .c_out(somador_1bit_5_c_out));
  somador_1bit somador_1bit_6 (
    .a(a[5]), .b(b[5]), .c_in(somador_1bit_5_c_out), .o(saida[5]), .c_out(somador_1bit_6_c_out));
  somador_1bit somador_1bit_7 (
    .a(a[6]), .b(b[6]), .c_in(somador_1bit_6_c_out), .o(saida[6]), .c_out(somador_1bit_7_c_out));
  somador_1bit somador_1bit_8 (.a(a[7]), .b(b[7]), .c_in(somador_1bit_7_c_out), .o(saida[7]), .c_out(out_5));
endmodule

module main_1bit (
  input  in_1,
  input  in_2,
  output out_3
);

  wire nand_1_out, nand_2_out, nand_4_out;

  nand nand_1 (nand_1_out, in_1, in_2);
  nand nand_2 (nand_2_out, nand_1_out, in_2);
  nand nand_3 (out_3, nand_1_out, nand_4_out);
  nand nand_4 (nand_4_out, out_3, nand_2_out);
endmodule

module registrador (
  input  [7:0] in_1,
  input  in_2,
  input  in_3,
  output [7:0] out_4
);

  wire main_1bit_1_out_3, main_1bit_2_out_3, main_1bit_3_out_3, main_1bit_4_out_3, main_1bit_5_out_3,
       main_1bit_6_out_3, main_1bit_7_out_3, main_1bit_8_out_3;

  main_1bit main_1bit_1 (.in_1(in_1[0]), .in_2(in_2), .out_3(main_1bit_1_out_3));
  main_1bit main_1bit_2 (.in_1(in_1[1]), .in_2(in_2), .out_3(main_1bit_2_out_3));
  main_1bit main_1bit_3 (.in_1(in_1[2]), .in_2(in_2), .out_3(main_1bit_3_out_3));
  main_1bit main_1bit_4 (.in_1(in_1[3]), .in_2(in_2), .out_3(main_1bit_4_out_3));
  main_1bit main_1bit_5 (.in_1(in_1[4]), .in_2(in_2), .out_3(main_1bit_5_out_3));
  main_1bit main_1bit_6 (.in_1(in_1[5]), .in_2(in_2), .out_3(main_1bit_6_out_3));
  main_1bit main_1bit_7 (.in_1(in_1[6]), .in_2(in_2), .out_3(main_1bit_7_out_3));
  main_1bit main_1bit_8 (.in_1(in_1[7]), .in_2(in_2), .out_3(main_1bit_8_out_3));
  and and_1 (out_4[0], main_1bit_1_out_3, in_3);
  and and_2 (out_4[1], main_1bit_2_out_3, in_3);
  and and_3 (out_4[2], main_1bit_3_out_3, in_3);
  and and_4 (out_4[3], main_1bit_4_out_3, in_3);
  and and_5 (out_4[4], main_1bit_5_out_3, in_3);
  and and_6 (out_4[5], main_1bit_6_out_3, in_3);
  and and_7 (out_4[6], main_1bit_7_out_3, in_3);
  and and_8 (out_4[7], main_1bit_8_out_3, in_3);
endmodule

module shift_Left (
  input  c_in,
  input  [15:0] in_2,
  output [15:0] out_3,
  output c_out
);


  assign c_out = in_2[15];
  assign out_3 = {in_2[14:0], c_in};
endmodule

module ULA (
  input  [2:0] in_1,
  input  [15:0] A,
  input  [15:0] B,
  output carry_out,
  output [15:0] out_5,
  output A_maior,
  output a_igual_b,
  output zero
);

  wire adder_1_cout, left_c_out, or_2_out, right_c_out;
  wire [15:0] adder_1_out, and_1_out, left_out_3, not_1_out, or_1_out, right_out_3, xor_1_out;

  Adder #(.width(16)) adder_1 (.a(A), .b(B), .out(adder_1_out), .cin(1'b0), .cout(adder_1_cout));
  shift_Right right (.in_1(A), .c_in(1'b0), .c_out(right_c_out), .out_3(right_out_3));
  shift_Left left (.in_2(A), .c_in(1'b0), .c_out(left_c_out), .out_3(left_out_3));
  assign not_1_out = ~A;  // NOT_Gate not_1, 16 bits wide
  assign and_1_out = A & B;  // AND_Gate and_1, 16 bits wide
  assign or_1_out = A | B;  // OR_Gate or_1, 16 bits wide
  assign xor_1_out = A ^ B;  // XOR_Gate xor_1, 16 bits wide
  Comparator #(.width(16)) comparator_1 (.a(A), .b(B), .gt(A_maior), .eq(a_igual_b));  // open: lt
  Multiplexer #(.select(3), .width(16)) multiplexer_1 (
    .in0(adder_1_out), .in1(right_out_3), .in2(left_out_3), .in3(not_1_out), .in4(and_1_out), .in5(or_1_out),
    .in6(xor_1_out), .in7(A), .out(out_5), .sel(in_1));
  Multiplexer #(.select(3)) multiplexer_2 (
    .in0(adder_1_cout), .in1(right_c_out), .in2(left_c_out), .in3(1'b0), .in4(1'b0), .in5(1'b0), .in6(1'b0),
    .in7(1'b0), .out(carry_out), .sel(in_1));
  or or_2 (or_2_out, out_5[0], out_5[1], out_5[2], out_5[3], out_5[4], out_5[5], out_5[6], out_5[7], out_5[8], out_5[9], out_5[10], out_5[11], out_5[12], out_5[13], out_5[14], out_5[15]);
  not not_2 (zero, or_2_out);
endmodule

module shift_Right (
  input  [15:0] in_1,
  input  c_in,
  output [15:0] out_3,
  output c_out
);


  assign c_out = in_1[0];
  assign out_3 = {c_in, in_1[15:1]};
endmodule

module ClK (
  output clk_s,
  output out_2,
  output clk_e
);

  wire clk_d_out;

  Clock #(.highDuration(2), .lowDuration(2)) main_clk (.out(out_2));
  Clock #(.highDuration(2), .lowDuration(2), .phaseOffset(3)) clk_d (.out(clk_d_out));
  and and_1 (clk_s, clk_d_out, out_2);
  or or_1 (clk_e, out_2, clk_d_out);
endmodule

module stepper (
  input  in_1,
  output out_2,
  output out_3,
  output out_4,
  output out_5,
  output out_6,
  output out_7,
  output out_8
);

  wire decoder_1_out7;
  wire [2:0] counter_1_q;

  Counter #(.max('h7), .width(3)) counter_1 (
    .D(counter_1_q), .Q(counter_1_q), .clk(in_1), .clr(decoder_1_out7));  // open: load, count, carry, up
  Decoder #(.enable("false"), .select(3)) decoder_1 (
    .out0(out_2), .out1(out_3), .out2(out_4), .out3(out_5), .out4(out_6), .out5(out_7), .out6(out_8),
    .out7(decoder_1_out7), .sel(counter_1_q));
endmodule

module UC (
  input  from_carry_out,
  input  flag_a_larger,
  input  reg_equal,
  input  reg_zero,
  input  [15:0] in_5,
  output r2_s,
  output r2_e,
  output r3_s,
  output r3_e,
  output to_mar_s,
  output to_tmp_s,
  output r0_s,
  output r0_e,
  output r1_s,
  output r1_e,
  output to_bus,
  output [2:0] ULA_OP,
  output to_ram_s,
  output to_ram_e,
  output inf,
  output to_flag_s,
  output to_acc_s,
  output to_acc_e,
  output to_iar_s,
  output to_iar_e,
  output ir_set,
  output input_output,
  output data_address,
  output to_io_e,
  output to_io_s
);

  wire A_out, and_8_out, and_9_out, and_10_out, and_11_out, and_12_out, and_13_out, and_14_out, and_15_out,
       and_16_out, and_17_out, and_18_out, and_19_out, and_20_out, and_21_out, and_22_out, and_23_out,
       and_24_out, and_25_out, and_26_out, and_27_out, C_out, clk_1_out_2, CLK_E, CLK_s, decoder_1_out0,
       decoder_1_out1, decoder_1_out2, decoder_1_out3, decor3x8_1_out_5, decor3x8_1_out_6, decor3x8_1_out_7,
       decor3x8_1_out_8, decor3x8_1_out_9, decor3x8_1_out_10, decor3x8_1_out_11, decor3x8_1_out_12,
       decor3x8_1_out_13, E_out, not_1_out, not_2_out, or_2_out, or_3_out, or_4_out, or_5_out, or_6_out,
       or_7_out, or_8_out, or_9_out, or_10_out, or_11_out, or_12_out, S1, S2, S3, S4, S5, S6, Z_out;

  and and_1 (to_iar_e, or_2_out, CLK_E);
  and and_2 (to_ram_e, or_3_out, CLK_E);
  and and_3 (to_acc_e, or_4_out, CLK_E);
  and and_4 (to_io_e, and_23_out, CLK_E);
  decor2x4 decor2x4_1 (
    .out_8(r0_e), .out_9(r1_e), .out_10(r2_e), .out_11(r3_e), .in_1(CLK_E), .in_2(or_5_out), .in_3(or_6_out),
    .in_4(in_5[0]), .in_5(in_5[1]), .in_6(in_5[2]), .in_7(in_5[3]));
  ClK clk_1 (.clk_s(CLK_s), .out_2(clk_1_out_2), .clk_e(CLK_E));
  or or_1 (to_bus, S1, and_15_out, and_14_out, and_11_out);
  or or_2 (or_2_out, S1, and_11_out, and_13_out, and_14_out);
  or or_3 (or_3_out, S2, and_27_out, and_21_out, and_20_out, and_18_out);
  or or_4 (or_4_out, S3, and_22_out, and_26_out, and_25_out);
  or or_5 (or_5_out, and_8_out, and_19_out, and_12_out, and_16_out);
  or or_6 (or_6_out, and_10_out, and_9_out, and_17_out);
  and and_5 (ULA_OP[0], S5, in_5[7], in_5[4]);
  and and_6 (ULA_OP[1], S5, in_5[7], in_5[5]);
  and and_7 (ULA_OP[2], S5, in_5[7], in_5[6]);
  decor3x8 decor3x8_1 (
    .out_5(decor3x8_1_out_5), .in_4(in_5[7]), .in_1(in_5[6]), .in_2(in_5[5]), .in_3(in_5[4]),
    .out_6(decor3x8_1_out_6), .out_7(decor3x8_1_out_7), .out_8(decor3x8_1_out_8), .out_9(decor3x8_1_out_9),
    .out_10(decor3x8_1_out_10), .out_11(decor3x8_1_out_11), .out_12(decor3x8_1_out_12),
    .out_13(decor3x8_1_out_13));
  stepper stepper_1 (
    .in_1(clk_1_out_2), .out_3(S1), .out_4(S2), .out_5(S3), .out_6(S4), .out_7(S5), .out_8(S6), .out_2(inf));
  and and_8 (and_8_out, S4, decor3x8_1_out_5);
  and and_9 (and_9_out, S4, decor3x8_1_out_6);
  and and_10 (and_10_out, S4, decor3x8_1_out_7);
  and and_11 (and_11_out, S4, decor3x8_1_out_8);
  and and_12 (and_12_out, S4, decor3x8_1_out_9);
  and and_13 (and_13_out, S4, decor3x8_1_out_10);
  and and_14 (and_14_out, S4, decor3x8_1_out_11);
  and and_15 (and_15_out, S4, decor3x8_1_out_12);
  and and_16 (and_16_out, S4, decor3x8_1_out_13, in_5[3]);
  not not_1 (not_1_out, in_5[3]);
  and and_17 (and_17_out, S5, decor3x8_1_out_5);
  and and_18 (and_18_out, S5, decor3x8_1_out_6);
  and and_19 (and_19_out, S5, decor3x8_1_out_7);
  and and_20 (and_20_out, S5, decor3x8_1_out_8);
  and and_21 (and_21_out, S5, decor3x8_1_out_10);
  and and_22 (and_22_out, S5, decor3x8_1_out_11);
  and and_23 (and_23_out, S5, decor3x8_1_out_13, not_1_out);
  and C (C_out, in_5[3], from_carry_out);
  and A (A_out, in_5[2], flag_a_larger);
  and E (E_out, in_5[1], reg_equal);
  and Z (Z_out, in_5[0], reg_zero);
  and and_24 (and_24_out, in_5[4], in_5[5], in_5[6]);
  or or_7 (or_7_out, C_out, A_out, E_out, Z_out);
  not not_2 (not_2_out, and_24_out);
  and and_25 (and_25_out, S6, decor3x8_1_out_5, not_2_out);
  and and_26 (and_26_out, S6, decor3x8_1_out_8);
  and and_27 (and_27_out, S6, decor3x8_1_out_11, or_7_out);
  or or_8 (or_8_out, S1, and_11_out, and_14_out, and_9_out, and_10_out, and_13_out);
  or or_9 (or_9_out, S3, and_12_out, and_21_out, and_22_out, and_26_out, and_27_out);
  or or_10 (or_10_out, S1, and_11_out, and_14_out, and_17_out);
  or or_11 (or_11_out, and_15_out, and_17_out);
  or or_12 (or_12_out, and_18_out, and_25_out, and_20_out, and_23_out);
  Decoder #(.enable("false"), .select(2)) decoder_1 (
    .out0(decoder_1_out0), .out1(decoder_1_out1), .out2(decoder_1_out2), .out3(decoder_1_out3),
    .sel(in_5[1:0]));
  and and_28 (ir_set, CLK_s, S2);
  and and_29 (to_mar_s, CLK_s, or_8_out);
  and and_30 (to_iar_s, CLK_s, or_9_out);
  and and_31 (to_acc_s, CLK_s, or_10_out);
  and and_32 (to_ram_s, CLK_s, and_19_out);
  and and_33 (to_tmp_s, CLK_s, and_8_out);
  and and_34 (to_flag_s, CLK_s, or_11_out);
  and and_35 (to_io_s, CLK_s, and_16_out);
  and and_36 (r0_s, CLK_s, or_12_out, decoder_1_out0);
  and and_37 (r1_s, CLK_s, or_12_out, decoder_1_out1);
  and and_38 (r2_s, CLK_s, or_12_out, decoder_1_out2);
  and and_39 (r3_s, CLK_s, or_12_out, decoder_1_out3);

  assign data_address = in_5[2];
  assign in_5[14:8] = {7{in_5[15]}};
  assign input_output = in_5[3];
  // also tied to GND on the sheet: in_5[15]

  // Other names for the same wires on the sheet: IR[15:0] = {{8{in_5[15]}}, in_5[7:0]}; init = inf; ULA[2:0] = ULA_OP
endmodule

// b1
module bus1 (
  input  [15:0] in_1,
  input  in_2,
  output [15:0] out_3
);

  Multiplexer #(.width(16)) multiplexer_1 (.in0(in_1), .in1(16'h1), .out(out_3), .sel(in_2));
endmodule

// flag
module Flag (
  input  in_1,
  input  in_2,
  input  in_3,
  input  in_4,
  input  in_5,
  output out_6,
  output out_7,
  output out_8,
  output out_9
);

  Register #(.width(4)) register_1 (
    .D({in_4, in_3, in_2, in_1}), .Q({out_9, out_8, out_7, out_6}), .clk(in_5));  // open: en, clr
endmodule

module decor3x8 (
  input  in_1,
  input  in_2,
  input  in_3,
  input  in_4,
  output out_5,
  output out_6,
  output out_7,
  output out_8,
  output out_9,
  output out_10,
  output out_11,
  output out_12,
  output out_13
);

  wire decoder_1_out0, decoder_1_out1, decoder_1_out2, decoder_1_out3, decoder_1_out4, decoder_1_out5,
       decoder_1_out6, decoder_1_out7, not_1_out;
  wire [0:0] undriven;

  not not_1 (not_1_out, in_4);
  // NOT_Gate not_2 is placed but not wired
  Decoder #(.enable("false"), .select(3)) decoder_1 (
    .out0(decoder_1_out0), .out1(decoder_1_out1), .out2(decoder_1_out2), .out3(decoder_1_out3),
    .out4(decoder_1_out4), .out5(decoder_1_out5), .out6(decoder_1_out6), .out7(decoder_1_out7),
    .sel({in_1, in_2, in_3}));
  Decoder #(.enable("false"), .select(3)) decoder_2 (
    .out0(decoder_1_out1), .out1(decoder_1_out2), .out2(decoder_1_out3), .out3(decoder_1_out4),
    .out4(decoder_1_out5), .out5(decoder_1_out6), .out6(decoder_1_out7), .sel({in_2, in_3, undriven[0]}));  // open: out7
  and and_1 (out_6, not_1_out, decoder_1_out0);
  // AND_Gate and_2 is placed but not wired
  and and_3 (out_7, not_1_out, decoder_1_out1);
  // AND_Gate and_4 is placed but not wired
  and and_5 (out_8, not_1_out, decoder_1_out2);
  // AND_Gate and_6 is placed but not wired
  and and_7 (out_9, not_1_out, decoder_1_out3);
  // AND_Gate and_8 is placed but not wired
  and and_9 (out_10, not_1_out, decoder_1_out4);
  // AND_Gate and_10 is placed but not wired
  and and_11 (out_11, not_1_out, decoder_1_out5);
  // AND_Gate and_12 is placed but not wired
  and and_13 (out_12, not_1_out, decoder_1_out6);
  // AND_Gate and_14 is placed but not wired
  and and_15 (out_13, not_1_out, decoder_1_out7);
  // AND_Gate and_16 is placed but not wired

  assign out_5 = in_4;
endmodule

module decor2x4 (
  input  in_1,
  input  in_2,
  input  in_3,
  input  in_4,
  input  in_5,
  input  in_6,
  input  in_7,
  output out_8,
  output out_9,
  output out_10,
  output out_11
);

  wire and_1_out, and_2_out, and_3_out, and_4_out, and_5_out, and_6_out, and_7_out, and_8_out,
       decoder_1_out0, decoder_1_out1, decoder_1_out2, decoder_1_out3, decoder_2_out0, decoder_2_out1,
       decoder_2_out2, decoder_2_out3;

  or or_1 (out_8, and_1_out, and_5_out);
  or or_2 (out_9, and_2_out, and_6_out);
  or or_3 (out_10, and_3_out, and_7_out);
  or or_4 (out_11, and_4_out, and_8_out);
  and and_1 (and_1_out, in_1, in_2, decoder_1_out0);
  and and_2 (and_2_out, in_1, in_2, decoder_1_out1);
  and and_3 (and_3_out, in_1, in_2, decoder_1_out2);
  and and_4 (and_4_out, in_1, in_2, decoder_1_out3);
  and and_5 (and_5_out, in_1, in_3, decoder_2_out0);
  and and_6 (and_6_out, in_1, in_3, decoder_2_out1);
  and and_7 (and_7_out, in_1, in_3, decoder_2_out2);
  and and_8 (and_8_out, in_1, in_3, decoder_2_out3);
  Decoder #(.enable("false"), .select(2)) decoder_1 (
    .out0(decoder_1_out0), .out1(decoder_1_out1), .out2(decoder_1_out2), .out3(decoder_1_out3),
    .sel({in_5, in_4}));
  Decoder #(.enable("false"), .select(2)) decoder_2 (
    .out0(decoder_2_out0), .out1(decoder_2_out1), .out2(decoder_2_out2), .out3(decoder_2_out3),
    .sel({in_7, in_6}));
endmodule
